// Logisim project CPU.circ as structural Verilog: 17 circuits, main circuit Processor
module Processor (
);

  wire and_1_out, and_2_out, and_3_out, and_4_out, businterface_1_bm0, businterface_1_bm1,
       businterface_1_bm2, businterface_1_bm3, businterface_1_ealign, businterface_1_nrw,
       businterface_1_strobe, button_1_out, button_2_out, button_3_out, button_4_out, button_5_out, CLK,
       clock_1_out, EALIGN, EQ, FETCH, fetchunit_1_id, fetchunit_1_ldsx, fetchunit_1_load0,
       fetchunit_1_load1, fetchunit_1_pce, fetchunit_1_store0, fetchunit_1_store1, ILL,
       instructionvalidator_1_ill, INT, IOE, JMP, LD, LD0, LD1, LNK, loadstoreunit_1_nop, LSX, LT, LTU, N0,
       N1, N2, nBUSY, not_1_out, not_2_out, not_3_out, OPI, or_2_out, PCR, programcounter_1_ealign, RDY, RST,
       RWE, SLT, SLU, ST0, ST1, SUP;
  wire [1:0] operandsequencer_1_s1, operandsequencer_1_s2;
  wire [3:0] AOP;
  wire [4:0] RD, registerdecoder_1_rd, RS1, RS2;
  wire [15:0] businterface_1_a;
  wire [29:16] businterface_1_a_2;
  wire [31:0] AR, bit_extender_1_out, DIN, fetchunit_1_addr, fetchunit_1_instr, fetchunit_1_npc,
       fetchunit_1_pc, fetchunit_1_tap, IMM, MD, multiplexer_1_out, multiplexer_2_out, multiplexer_3_out,
       NPC, PC, programcounter_1_pc, ram_1_data, rom_1_data, RV, RX, RY, shifter_1_out, stagebuffer_1_instr,
       stagebuffer_1_instr_out, stagebuffer_1_npc_out, stagebuffer_1_pc, stagebuffer_1_pc_out,
       stagebuffer_2_instr, stagebuffer_2_instr_out, stagebuffer_2_npc_out, stagebuffer_2_pc_out,
       stagebuffer_3_instr, stagebuffer_3_instr_out, stagebuffer_3_pc, X, Y;

  not not_1 (not_1_out, not_3_out);
  and and_1 (and_1_out, 1'b1, businterface_1_a_2[29], businterface_1_a_2[28], businterface_1_a_2[27], businterface_1_a_2[26], businterface_1_a_2[25], businterface_1_a_2[24], businterface_1_a_2[23], businterface_1_a_2[22], businterface_1_a_2[21], businterface_1_a_2[20], businterface_1_a_2[19], businterface_1_a_2[18], businterface_1_a_2[17], businterface_1_a_2[16]);
  not not_2 (not_2_out, and_1_out);
  and and_2 (and_2_out, not_1_out, not_2_out);
  and and_3 (and_3_out, not_2_out, not_3_out);
  ROM #(.addrWidth(16), .dataWidth(32)) rom_1 (.addr(businterface_1_a), .data(rom_1_data));
  RAM #(.addrWidth(16), .asyncread("true"), .byteenables("byteEnables"), .dataWidth(32), .databus("bidir"), .trigger("falling")) ram_1 (
    .addr(businterface_1_a), .we(and_2_out), .oe(and_3_out), .clk(businterface_1_strobe), .data(ram_1_data),
    .be3(businterface_1_bm3), .be2(businterface_1_bm2), .be1(businterface_1_bm1), .be0(businterface_1_bm0));
  assign bit_extender_1_out = {{2{businterface_1_a_2[29]}}, {businterface_1_a_2, businterface_1_a}};  // Bit_Extender bit_extender_1
  // Probe on shifter_1_out
  Shifter #(.width(32)) shifter_1 (.in(bit_extender_1_out), .\dist (5'b00010), .out(shifter_1_out));
  // Probe on ram_1_data
  assign ram_1_data = and_4_out ? rom_1_data : 32'bz;  // Controlled_Buffer controlled_buffer_1
  and and_4 (and_4_out, and_1_out, not_3_out);
  not not_3 (not_3_out, businterface_1_nrw);
  BusInterface businterface_1 (
    .STROBE(businterface_1_strobe), .RDY(RDY), .A({businterface_1_a_2, businterface_1_a}),
    .EALIGN(businterface_1_ealign), .BM0(businterface_1_bm0), .BM1(businterface_1_bm1),
    .BM2(businterface_1_bm2), .BM3(businterface_1_bm3), .nRW(businterface_1_nrw), .DO(ram_1_data), .DIN(DIN),
    .ADDR(fetchunit_1_addr), .LOAD0(fetchunit_1_load0), .LOAD1(fetchunit_1_load1),
    .STORE0(fetchunit_1_store0), .STORE1(fetchunit_1_store1), .CLK(CLK), .DI(ram_1_data), .DOUT(MD),
    .LDSX(fetchunit_1_ldsx), .LD(LD), .RST(RST), .nBUSY(nBUSY));
  RegisterFile registerfile_1 (.X(RX), .Y(RY), .YI(RS2), .WE(RWE), .CLK(CLK), .D(multiplexer_1_out), .WI(RD), .XI(RS1));
  Multiplexer #(.width(32)) multiplexer_1 (.in0(RV), .in1(NPC), .out(multiplexer_1_out), .sel(LNK));
  or or_1 (EALIGN, businterface_1_ealign, programcounter_1_ealign);
  FetchUnit fetchunit_1 (
    .NPC(fetchunit_1_npc), .PC(fetchunit_1_pc), .ILL(ILL), .TAP(fetchunit_1_tap), .INSTR(fetchunit_1_instr),
    .ADDR(fetchunit_1_addr), .ID(fetchunit_1_id), .PCE(fetchunit_1_pce), .LDSX(fetchunit_1_ldsx),
    .LOAD0(fetchunit_1_load0), .LOAD1(fetchunit_1_load1), .LOAD(LD), .STORE0(fetchunit_1_store0),
    .STORE1(fetchunit_1_store1), .DIN(DIN), .NOP(N0), .RST(RST), .CLK(CLK),
    .ILL_IN(instructionvalidator_1_ill), .BUS_RDY(RDY), .SX(LSX), .LD0(LD0), .LD1(LD1), .ST0(ST0), .ST1(ST1),
    .FETCH(FETCH), .IO(IOE), .IPC(programcounter_1_pc), .EMA(RV));
  InstructionValidator instructionvalidator_1 (
    .ILL(instructionvalidator_1_ill), .INSTR(fetchunit_1_tap), .ID(fetchunit_1_id));
  ProgramCounter programcounter_1 (
    .EALIGN(programcounter_1_ealign), .PC(programcounter_1_pc), .CLK(CLK), .ADDR(RV), .JMP(JMP),
    .INT(or_2_out), .PCE(fetchunit_1_pce));
  StageBuffer stagebuffer_1 (
    .PC(stagebuffer_1_pc), .PC_OUT(stagebuffer_1_pc_out), .NPC_OUT(stagebuffer_1_npc_out),
    .INSTR(stagebuffer_1_instr), .INSTR_OUT(stagebuffer_1_instr_out), .NOP_OUT(N0), .SUP(SUP), .CLK(CLK),
    .NOP(1'b0), .NOP_IN(N1), .PC_IN(fetchunit_1_pc), .NPC_IN(fetchunit_1_npc), .INSTR_IN(fetchunit_1_instr));
  or or_2 (or_2_out, INT, RST);
  RegisterDecoder registerdecoder_1 (.RD(registerdecoder_1_rd), .RS1(RS1), .RS2(RS2), .INSTR(stagebuffer_1_instr));
  OperandSequencer operandsequencer_1 (
    .S1(operandsequencer_1_s1), .S2(operandsequencer_1_s2), .RS1(RS1), .WE(RWE), .WR(RD), .RS2(RS2),
    .CLK(CLK), .NOP(N0), .RD(registerdecoder_1_rd));
  // NoConnect on stagebuffer_1_pc
  // Probe on stagebuffer_1_instr
  ArithmeticDecoder arithmeticdecoder_1 (
    .IMM(IMM), .PCREL(PCR), .OPIMM(OPI), .SLT(SLT), .SLTU(SLU), .ALU_OP(AOP), .INSTR(stagebuffer_2_instr));
  Multiplexer #(.width(32)) multiplexer_2 (.in0(X), .in1(PC), .out(multiplexer_2_out), .sel(PCR));
  Multiplexer #(.width(32)) multiplexer_3 (.in0(Y), .in1(IMM), .out(multiplexer_3_out), .sel(OPI));
  StageBuffer stagebuffer_2 (
    .PC(PC), .PC_OUT(stagebuffer_2_pc_out), .NPC_OUT(stagebuffer_2_npc_out), .INSTR(stagebuffer_2_instr),
    .INSTR_OUT(stagebuffer_2_instr_out), .NOP_OUT(N1), .SUP(SUP), .CLK(CLK), .NOP(1'b0), .NOP_IN(N2),
    .PC_IN(stagebuffer_1_pc_out), .NPC_IN(stagebuffer_1_npc_out), .INSTR_IN(stagebuffer_1_instr_out));
  OperandMux operandmux_1 (
    .OUT_X(X), .OUT_Y(Y), .SEL_X(operandsequencer_1_s1), .REG_X(RX), .ALU_OUT(AR), .MEM_IN(RV), .REG_Y(RY),
    .SEL_Y(operandsequencer_1_s2), .CLK(CLK));
  ALU alu_1 (
    .R(AR), .SEL(AOP), .X(multiplexer_2_out), .Y(multiplexer_3_out), .SLT(SLT), .SLTU(SLU), .CLK(CLK),
    .NOP(N1));
  // Probe on stagebuffer_2_instr
  StageBuffer stagebuffer_3 (
    .PC(stagebuffer_3_pc), .NPC_OUT(NPC), .INSTR(stagebuffer_3_instr), .INSTR_OUT(stagebuffer_3_instr_out),
    .NOP_OUT(N2), .SUP(SUP), .CLK(CLK), .NOP(loadstoreunit_1_nop), .NOP_IN(1'b0),
    .PC_IN(stagebuffer_2_pc_out), .NPC_IN(stagebuffer_2_npc_out), .INSTR_IN(stagebuffer_2_instr_out));  // open: PC_OUT
  LoadStoreUnit loadstoreunit_1 (
    .ST0(ST0), .ST1(ST1), .LD1(LD1), .SX(LSX), .LD0(LD0), .NOP(loadstoreunit_1_nop), .IOE(IOE),
    .INSTR(stagebuffer_3_instr), .CLK(CLK), .RDY(RDY), .RST(RST));
  // NoConnect on stagebuffer_3_pc
  // Probe on stagebuffer_3_instr
  BranchController branchcontroller_1 (
    .JMP(JMP), .SUP(SUP), .LINK(LNK), .WE(RWE), .RD(RD), .INSTR(stagebuffer_3_instr_out), .EQ(EQ), .LT(LT),
    .LTU(LTU), .CLK(CLK));
  ResultBuffer resultbuffer_1 (
    .VAL(RV), .Y(MD), .EQ(EQ), .LT(LT), .LTU(LTU), .D_IN(DIN), .X_IN(X), .Y_IN(Y), .CLK(CLK), .NOP(N2),
    .V_IN(AR), .LD(LD));
  Clock clock_1 (.out(clock_1_out));
  or or_3 (CLK, clock_1_out, button_1_out);
  Button button_1 (.out(button_1_out));
  T_Flip_Flop t_ff_1 (.T(1'b1), .clk(button_2_out), .Qn(RST));  // open: Q, reset, preset
  Button button_2 (.out(button_2_out));
  T_Flip_Flop t_ff_2 (.T(1'b1), .clk(button_3_out), .Q(INT));  // open: Qn, reset, preset
  Button button_3 (.out(button_3_out));
  T_Flip_Flop t_ff_3 (.T(1'b1), .clk(button_4_out), .Qn(FETCH));  // open: Q, reset, preset
  Button button_4 (.out(button_4_out));
  T_Flip_Flop t_ff_4 (.T(1'b1), .clk(button_5_out), .Qn(nBUSY));  // open: Q, reset, preset
  Button button_5 (.out(button_5_out));

  // Notes on the sheet:
  //   contents of rom_1 (hex, n*v repeats v):
  //   fffc07b7 87a783 f4637 23e60613 100793 100713 f706b3 fed66ae3 78713 68793 ff1ff06f 65521*0 10000113
  //   fffc00b7 8067
endmodule

module RegisterFile (
  input  [4:0] WI,
  input  [31:0] D,
  input  WE,
  input  CLK,
  input  [4:0] XI,
  input  [4:0] YI,
  output [31:0] X,
  output [31:0] Y
);

  wire NCLK, W0, W1, W2, W3, W4, W5, W6, W7, W8, W9, W10, W11, W12, W13, W14, W15, W16, W17, W18, W19, W20,
       W21, W22, W23, W24, W25, W26, W27, W28, W29, W30, W31, WR;
  wire [31:0] decoder_1_out0, decoder_4_out0, L0_p2, multiplexer_1_out, multiplexer_2_out, R1, R2, R3, R4,
       R5, R6, R7, R8, R9, R10, R11, R12, R13, R14, R15, R16, R17, R18, R19, R20, R21, R22, R23, R24, R25,
       R26, R27, R28, R29, R30, R31;

  Decoder #(.enable("false"), .select(5)) decoder_1 (
    .out0(decoder_1_out0[0]), .out1(decoder_1_out0[1]), .out2(decoder_1_out0[2]), .out3(decoder_1_out0[3]),
    .out4(decoder_1_out0[4]), .out5(decoder_1_out0[5]), .out6(decoder_1_out0[6]), .out7(decoder_1_out0[7]),
    .out8(decoder_1_out0[8]), .out9(decoder_1_out0[9]), .out10(decoder_1_out0[10]),
    .out11(decoder_1_out0[11]), .out12(decoder_1_out0[12]), .out13(decoder_1_out0[13]),
    .out14(decoder_1_out0[14]), .out15(decoder_1_out0[15]), .out16(decoder_1_out0[16]),
    .out17(decoder_1_out0[17]), .out18(decoder_1_out0[18]), .out19(decoder_1_out0[19]),
    .out20(decoder_1_out0[20]), .out21(decoder_1_out0[21]), .out22(decoder_1_out0[22]),
    .out23(decoder_1_out0[23]), .out24(decoder_1_out0[24]), .out25(decoder_1_out0[25]),
    .out26(decoder_1_out0[26]), .out27(decoder_1_out0[27]), .out28(decoder_1_out0[28]),
    .out29(decoder_1_out0[29]), .out30(decoder_1_out0[30]), .out31(decoder_1_out0[31]), .sel(XI));
  // RGBLED L31: pin names not known; wires that end beside it: decoder_1_out0[31], L0_p2[31]
  // RGBLED L30: pin names not known; wires that end beside it: decoder_1_out0[30], L0_p2[30]
  and and_1 (WR, WE, CLK);
  not not_1 (NCLK, CLK);
  // RGBLED L29: pin names not known; wires that end beside it: decoder_1_out0[29], L0_p2[29]
  // RGBLED L28: pin names not known; wires that end beside it: decoder_1_out0[28], L0_p2[28]
  Register #(.width(32)) register_1 (.D(D), .clk(W1), .Q(R1));  // open: en, clr
  Register #(.width(32)) register_2 (.D(D), .clk(W2), .Q(R2));  // open: en, clr
  Register #(.width(32)) register_3 (.D(D), .clk(W3), .Q(R3));  // open: en, clr
  Register #(.trigger("high"), .width(32)) register_4 (.D(D), .clk(1'b1));  // open: en, Q, clr
  // RGBLED L27: pin names not known; wires that end beside it: decoder_1_out0[27], L0_p2[27]
  // RGBLED L26: pin names not known; wires that end beside it: decoder_1_out0[26], L0_p2[26]
  // RGBLED L25: pin names not known; wires that end beside it: decoder_1_out0[25], L0_p2[25]
  Register #(.width(32)) register_5 (.D(D), .clk(W4), .Q(R4));  // open: en, clr
  Register #(.width(32)) register_6 (.D(D), .clk(W5), .Q(R5));  // open: en, clr
  Register #(.width(32)) register_7 (.D(D), .clk(W6), .Q(R6));  // open: en, clr
  Register #(.width(32)) register_8 (.D(D), .clk(W7), .Q(R7));  // open: en, clr
  Decoder #(.select(5)) decoder_2 (
    .out0(W0), .out1(W1), .out2(W2), .out3(W3), .out4(W4), .out5(W5), .out6(W6), .out7(W7), .out8(W8),
    .out9(W9), .out10(W10), .out11(W11), .out12(W12), .out13(W13), .out14(W14), .out15(W15), .out16(W16),
    .out17(W17), .out18(W18), .out19(W19), .out20(W20), .out21(W21), .out22(W22), .out23(W23), .out24(W24),
    .out25(W25), .out26(W26), .out27(W27), .out28(W28), .out29(W29), .out30(W30), .out31(W31), .sel(WI),
    .en(WR));
  // RGBLED L24: pin names not known; wires that end beside it: decoder_1_out0[24], L0_p2[24]
  // RGBLED L23: pin names not known; wires that end beside it: decoder_1_out0[23], L0_p2[23]
  // RGBLED L22: pin names not known; wires that end beside it: decoder_1_out0[22], L0_p2[22]
  Register #(.width(32)) register_9 (.D(D), .clk(W8), .Q(R8));  // open: en, clr
  Register #(.width(32)) register_10 (.D(D), .clk(W9), .Q(R9));  // open: en, clr
  Register #(.width(32)) register_11 (.D(D), .clk(W10), .Q(R10));  // open: en, clr
  Register #(.width(32)) register_12 (.D(D), .clk(W11), .Q(R11));  // open: en, clr
  // RGBLED L21: pin names not known; wires that end beside it: decoder_1_out0[21], L0_p2[21]
  // RGBLED L20: pin names not known; wires that end beside it: decoder_1_out0[20], L0_p2[20]
  // RGBLED L19: pin names not known; wires that end beside it: decoder_1_out0[19], L0_p2[19]
  // RGBLED L18: pin names not known; wires that end beside it: decoder_1_out0[18], L0_p2[18]
  Register #(.width(32)) register_13 (.D(D), .clk(W12), .Q(R12));  // open: en, clr
  Register #(.width(32)) register_14 (.D(D), .clk(W13), .Q(R13));  // open: en, clr
  Register #(.width(32)) register_15 (.D(D), .clk(W14), .Q(R14));  // open: en, clr
  Register #(.width(32)) register_16 (.D(D), .clk(W15), .Q(R15));  // open: en, clr
  // RGBLED L17: pin names not known; wires that end beside it: decoder_1_out0[17], L0_p2[17]
  Multiplexer #(.select(5), .width(32)) multiplexer_1 (
    .in0({32{1'b0}}), .in1(R1), .in2(R2), .in3(R3), .in4(R4), .in5(R5), .in6(R6), .in7(R7), .in8(R8),
    .in9(R9), .in10(R10), .in11(R11), .in12(R12), .in13(R13), .in14(R14), .in15(R15), .in16(R16), .in17(R17),
    .in18(R18), .in19(R19), .in20(R20), .in21(R21), .in22(R22), .in23(R23), .in24(R24), .in25(R25),
    .in26(R26), .in27(R27), .in28(R28), .in29(R29), .in30(R30), .in31(R31), .out(multiplexer_1_out), .sel(XI));
  // RGBLED L16: pin names not known; wires that end beside it: decoder_1_out0[16], L0_p2[16]
  // RGBLED L15: pin names not known; wires that end beside it: decoder_1_out0[15], L0_p2[15]
  Register #(.width(32)) register_17 (.D(D), .clk(W16), .Q(R16));  // open: en, clr
  Register #(.width(32)) register_18 (.D(D), .clk(W17), .Q(R17));  // open: en, clr
  Register #(.width(32)) register_19 (.D(D), .clk(W18), .Q(R18));  // open: en, clr
  Register #(.width(32)) register_20 (.D(D), .clk(W19), .Q(R19));  // open: en, clr
  Register #(.trigger("high"), .width(32)) RX (.D(multiplexer_1_out), .clk(NCLK), .Q(X));  // open: en, clr
  // RGBLED L14: pin names not known; wires that end beside it: decoder_1_out0[14], L0_p2[14]
  // RGBLED L13: pin names not known; wires that end beside it: decoder_1_out0[13], L0_p2[13]
  // RGBLED L12: pin names not known; wires that end beside it: decoder_1_out0[12], L0_p2[12]
  Register #(.width(32)) register_21 (.D(D), .clk(W20), .Q(R20));  // open: en, clr
  Register #(.width(32)) register_22 (.D(D), .clk(W21), .Q(R21));  // open: en, clr
  Register #(.width(32)) register_23 (.D(D), .clk(W22), .Q(R22));  // open: en, clr
  Register #(.width(32)) register_24 (.D(D), .clk(W23), .Q(R23));  // open: en, clr
  // RGBLED L11: pin names not known; wires that end beside it: decoder_1_out0[11], L0_p2[11]
  // RGBLED L10: pin names not known; wires that end beside it: decoder_1_out0[10], L0_p2[10]
  // RGBLED L9: pin names not known; wires that end beside it: decoder_1_out0[9], L0_p2[9]
  Register #(.width(32)) register_25 (.D(D), .clk(W24), .Q(R24));  // open: en, clr
  Register #(.width(32)) register_26 (.D(D), .clk(W25), .Q(R25));  // open: en, clr
  Register #(.width(32)) register_27 (.D(D), .clk(W26), .Q(R26));  // open: en, clr
  Register #(.width(32)) register_28 (.D(D), .clk(W27), .Q(R27));  // open: en, clr
  // RGBLED L8: pin names not known; wires that end beside it: decoder_1_out0[8], L0_p2[8]
  // RGBLED L7: pin names not known; wires that end beside it: decoder_1_out0[7], L0_p2[7]
  // RGBLED L6: pin names not known; wires that end beside it: decoder_1_out0[6], L0_p2[6]
  Register #(.width(32)) register_29 (.D(D), .clk(W28), .Q(R28));  // open: en, clr
  Register #(.width(32)) register_30 (.D(D), .clk(W29), .Q(R29));  // open: en, clr
  Register #(.width(32)) register_31 (.D(D), .clk(W30), .Q(R30));  // open: en, clr
  Register #(.width(32)) register_32 (.D(D), .clk(W31), .Q(R31));  // open: en, clr
  Multiplexer #(.select(5), .width(32)) multiplexer_2 (
    .in0({32{1'b0}}), .in1(R1), .in2(R2), .in3(R3), .in4(R4), .in5(R5), .in6(R6), .in7(R7), .in8(R8),
    .in9(R9), .in10(R10), .in11(R11), .in12(R12), .in13(R13), .in14(R14), .in15(R15), .in16(R16), .in17(R17),
    .in18(R18), .in19(R19), .in20(R20), .in21(R21), .in22(R22), .in23(R23), .in24(R24), .in25(R25),
    .in26(R26), .in27(R27), .in28(R28), .in29(R29), .in30(R30), .in31(R31), .out(multiplexer_2_out), .sel(YI));
  // RGBLED L5: pin names not known; wires that end beside it: decoder_1_out0[5], L0_p2[5]
  // RGBLED L4: pin names not known; wires that end beside it: decoder_1_out0[4], L0_p2[4]
  Register #(.trigger("high"), .width(32)) RY (.D(multiplexer_2_out), .clk(NCLK), .Q(Y));  // open: en, clr
  // RGBLED L3: pin names not known; wires that end beside it: decoder_1_out0[3], L0_p2[3]
  // RGBLED L2: pin names not known; wires that end beside it: decoder_1_out0[2], L0_p2[2]
  // RGBLED L1: pin names not known; wires that end beside it: decoder_1_out0[1], L0_p2[1]
  // RGBLED L0: pin names not known; wires that end beside it: decoder_1_out0[0], L0_p2[0]
  Decoder #(.enable("false"), .select(5)) decoder_3 (
    .out0(L0_p2[0]), .out1(L0_p2[1]), .out2(L0_p2[2]), .out3(L0_p2[3]), .out4(L0_p2[4]), .out5(L0_p2[5]),
    .out6(L0_p2[6]), .out7(L0_p2[7]), .out8(L0_p2[8]), .out9(L0_p2[9]), .out10(L0_p2[10]), .out11(L0_p2[11]),
    .out12(L0_p2[12]), .out13(L0_p2[13]), .out14(L0_p2[14]), .out15(L0_p2[15]), .out16(L0_p2[16]),
    .out17(L0_p2[17]), .out18(L0_p2[18]), .out19(L0_p2[19]), .out20(L0_p2[20]), .out21(L0_p2[21]),
    .out22(L0_p2[22]), .out23(L0_p2[23]), .out24(L0_p2[24]), .out25(L0_p2[25]), .out26(L0_p2[26]),
    .out27(L0_p2[27]), .out28(L0_p2[28]), .out29(L0_p2[29]), .out30(L0_p2[30]), .out31(L0_p2[31]), .sel(YI));
  Decoder #(.enable("false"), .select(5)) decoder_4 (
    .out0(decoder_4_out0[0]), .out1(decoder_4_out0[1]), .out2(decoder_4_out0[2]), .out3(decoder_4_out0[3]),
    .out4(decoder_4_out0[4]), .out5(decoder_4_out0[5]), .out6(decoder_4_out0[6]), .out7(decoder_4_out0[7]),
    .out8(decoder_4_out0[8]), .out9(decoder_4_out0[9]), .out10(decoder_4_out0[10]),
    .out11(decoder_4_out0[11]), .out12(decoder_4_out0[12]), .out13(decoder_4_out0[13]),
    .out14(decoder_4_out0[14]), .out15(decoder_4_out0[15]), .out16(decoder_4_out0[16]),
    .out17(decoder_4_out0[17]), .out18(decoder_4_out0[18]), .out19(decoder_4_out0[19]),
    .out20(decoder_4_out0[20]), .out21(decoder_4_out0[21]), .out22(decoder_4_out0[22]),
    .out23(decoder_4_out0[23]), .out24(decoder_4_out0[24]), .out25(decoder_4_out0[25]),
    .out26(decoder_4_out0[26]), .out27(decoder_4_out0[27]), .out28(decoder_4_out0[28]),
    .out29(decoder_4_out0[29]), .out30(decoder_4_out0[30]), .out31(decoder_4_out0[31]), .sel(WI));

  // Other names for the same wires on the sheet: DI[31:0] = D
endmodule

module ProgramCounter (
  input  JMP,
  input  INT,
  input  PCE,
  input  [31:0] ADDR,
  input  CLK,
  output EALIGN,
  output [31:0] PC
);

  wire not_1_out, not_2_out, or_1_out, or_2_out;
  wire [29:0] multiplexer_1_out;
  wire [31:0] register_1_q;

  Register #(.width(32)) register_1 (.D(ADDR), .clk(CLK), .Q(register_1_q));  // open: en, clr
  not not_1 (not_1_out, INT);
  and and_1 (EALIGN, or_2_out, or_1_out);
  or or_1 (or_1_out, JMP, INT);
  Multiplexer #(.width(30)) multiplexer_1 (
    .in0(30'h3ffffffc), .in1(register_1_q[31:2]), .out(multiplexer_1_out), .sel(not_1_out));
  or or_2 (or_2_out, register_1_q[1], register_1_q[0]);
  not not_2 (not_2_out, CLK);
  Counter #(.max('h3fffffff), .width(30)) counter_1 (
    .load(or_1_out), .count(PCE), .clk(not_2_out), .D(multiplexer_1_out), .Q(PC[31:2]));  // open: clr, up, carry
  Register #(.trigger("high"), .width(32)) register_2 (.D({PC[31:2], 2'b00}), .clk(1'b1));  // open: en, Q, clr

  assign PC[1:0] = 2'b00;
endmodule

module InstructionDecoder (
  input  [31:0] INSTR,
  input  CLK,
  input  EQ,
  input  LT,
  input  LTU,
  output STEP,
  output SIGILL,
  output JMP,
  output PCREL,
  output OPIMM,
  output REG_WE,
  output LINK,
  output SLT,
  output SLTU,
  output LDSX,
  output LOAD0,
  output [31:0] IMM,
  output LOAD1,
  output STORE0,
  output STORE1,
  output [3:0] ALU_OP,
  output SYSTEM,
  output [4:0] WI,
  output [4:0] XI,
  output [4:0] YI,
  output BREAK
);

  wire and_6_out, and_7_out, decoder_1_out0, decoder_1_out1, decoder_1_out2, decoder_1_out3,
       multiplexer_1_out, multiplexer_2_out, nand_1_out, nand_2_out, not_1_out, nSHIFT, or_2_out, or_3_out,
       P7, P30, P31, RD, RS1, RS2, S4_1_0, S4_1_1, S10_5, S19_12, S30_20, SIGILL_t;
  wire [0:0] IDEC_p3;
  wire [1:0] register_1_q, StageCounter_q;
  wire [2:0] and_4_out, FUNCT3, register_2_q;
  wire [3:0] and_8_out, and_9_out, P11_8;
  wire [4:0] OP, P30_25;
  wire [4:1] P24_20;
  wire [5:5] and_5_out;
  wire [7:3] P19_12;
  wire [8:3] CLF_p3;
  wire [9:9] xor_1_out;
  wire [20:17] MicroCode_data;

  Register #(.width(32)) register_1 (
    .D(INSTR), .clk(nand_1_out),
    .Q({P31, P30, P30_25, P24_20, BREAK, P19_12, FUNCT3, P11_8, P7, OP, register_1_q}));  // open: en, clr
  nand nand_1 (nand_1_out, STEP, CLK);
  Register #(.width(3)) register_2 (.D({LTU, LT, EQ}), .clk(CLK), .Q(register_2_q));  // open: en, clr
  Counter #(.max('h3), .width(2)) StageCounter (
    .load(STEP), .clk(not_1_out), .D(2'b00), .Q(StageCounter_q));  // open: clr, up, count, carry
  not not_1 (not_1_out, CLK);
  Multiplexer multiplexer_1 (.in0(register_2_q[1]), .in1(register_2_q[2]), .out(multiplexer_1_out), .sel(FUNCT3[1]));
  Multiplexer multiplexer_2 (.in0(register_2_q[0]), .in1(multiplexer_1_out), .out(multiplexer_2_out), .sel(FUNCT3[2]));
  LED COND (.in(xor_1_out[9]));
  LED S0 (.in(decoder_1_out0));
  LED S1 (.in(decoder_1_out1));
  LED S2 (.in(decoder_1_out2));
  LED S3 (.in(decoder_1_out3));
  nand nand_2 (nand_2_out, register_1_q[0], register_1_q[1]);
  // Probe on OP
  assign WI = {5{RD}} & {P11_8, P7};  // AND_Gate and_1, 5 bits wide
  // Probe on {P11_8, P7}
  // Probe on FUNCT3
  assign XI = {5{RS1}} & P19_12;  // AND_Gate and_2, 5 bits wide
  // Probe on P19_12
  assign YI = {5{RS2}} & {P24_20, BREAK};  // AND_Gate and_3, 5 bits wide
  // Probe on {P24_20, BREAK}
  // Probe on {P31, P30, P30_25}
  ROM #(.addrWidth(12), .dataWidth(21)) MicroCode (
    .addr({StageCounter_q, xor_1_out[9], P30, and_4_out, OP}),
    .data({MicroCode_data[20], SYSTEM, nSHIFT, MicroCode_data[17], ALU_OP, STORE1, STORE0, LOAD1, LOAD0, LDSX, SLTU, SLT, LINK, REG_WE, OPIMM, PCREL, JMP, STEP}));
  assign and_4_out = {3{RS1}} & FUNCT3;  // AND_Gate and_4, 3 bits wide
  xor xor_1 (xor_1_out[9], FUNCT3[0], multiplexer_2_out);
  Decoder #(.enable("false"), .select(2)) decoder_1 (
    .out0(decoder_1_out0), .out1(decoder_1_out1), .out2(decoder_1_out2), .out3(decoder_1_out3),
    .sel(StageCounter_q));
  // PlaRom #(.Contents("1 2 2 1 1 2 2 1 1 2*4 1*4 0 1*5 2 2 1 2 1*3 2 2 1*4 0 2 1 2*3 1 2 2 0 2 0 1*3 0 0 1 1 2 2 1 1 0 0 2 1*4 2 0 1*3 0 2 1 0 2 2 1 0 2 0 2 2 1 1 1 0*9 1 0*8 1 0*8 1 0*6 1 0 1 0*4 1 0 1 0 0 1 0*9 1 0*9 1 0*9 1 0*9 1 0*8 1 0*8 1 0*9 1 0*8 1 0*9 1 0*8 1 0*8 1"), .\and (17), .outputs(9)) CLF: pin names not known; wires that end beside it: OP, 1'b0, {CLF_p3, RS1, RS2, RD}
  LED R (.in(CLF_p3[8]));
  LED I (.in(CLF_p3[7]));
  LED S (.in(CLF_p3[6]));
  LED B (.in(CLF_p3[5]));
  LED U (.in(CLF_p3[4]));
  LED J (.in(CLF_p3[3]));
  // PlaRom #(.Contents("0 0 2 1 2 1*3 0 2 0 2*3 1 1 0 2 0 2 2 1 1 2 0 2 0 1*3 2 2 0 2 0 1 1 0 1 1 0*3 2*3 1 1 0*3 2 2 1 0 2 0*3 1*3 2 2 0*3 1 1 0 1 1 0*4 2 1*3 0*3 2 0*8 1 0 0 1 0*5 1 0*8 2 0*3 2*3 1*3 0 2 0 2 2 1 2*3 0 0 2 0*4 2 0*3 1 0 0 1 2 0*4 1 0 0 2 0*5 2 0*4 1 0 2 1 2 0*3 2 2 1 2*3 0*3 1 0*3 2 0*6 2 0*3 2 1 0*6 2 0 2 0 2 0*3 1 2 1 0 2 0*3 1 0 1 1 2 0*5 2 2 0*7 2 1 1 0*8 1 0*8 1 0*8 1 0*8 1 0*9 1 0*8 1 0*8 1 0*8 1 0*9 1 0*9 1 0*8 1 0*8 1 0*8 1 0*9 1 0*8 1 0*8 1 0 0 1 0*5 1 0*8 1 0 0 1 0*5 1 0 0 1 0*6 1 1 0*7 1 0*10 1 0*8 1 0*9 1 0*8 1 0*8 1 0*8 1 0*8 1 0*8 1"), .\and (30), .outputs(9)) IDEC: pin names not known; wires that end beside it: {P31, BREAK, P7, OP}, 1'b0, {IMM[0], S4_1_0, S4_1_1, S10_5, IMM[11], S19_12, S30_20, IMM[31], IDEC_p3[0]}
  or or_1 (SIGILL, nand_2_out, SIGILL_t, IDEC_p3[0]);
  or or_2 (or_2_out, P31, P30_25[4], P30_25[3], P30_25[2], P30_25[1], P30_25[0]);
  or or_3 (or_3_out, P24_20[4], P24_20[3], P24_20[2], P24_20[1]);
  and and_5 (and_5_out[5], S10_5, nSHIFT);
  and and_6 (and_6_out, or_2_out, MicroCode_data[17]);
  or or_4 (SIGILL_t, and_6_out, MicroCode_data[20], and_7_out);
  and and_7 (and_7_out, SYSTEM, or_3_out);
  assign and_8_out = {4{S4_1_1}} & P11_8;  // AND_Gate and_8, 4 bits wide
  assign and_9_out = {4{S4_1_0}} & P24_20;  // AND_Gate and_9, 4 bits wide
  Multiplexer #(.width(8)) multiplexer_3 (.in0({8{IMM[31]}}), .in1({P19_12, FUNCT3}), .out(IMM[19:12]), .sel(S19_12));
  Multiplexer #(.width(11)) multiplexer_4 (
    .in0({11{IMM[31]}}), .in1({P30, P30_25, P24_20, BREAK}), .out(IMM[30:20]), .sel(S30_20));
  assign IMM[4:1] = and_8_out | and_9_out;  // OR_Gate or_5, 4 bits wide
  assign IMM[10:5] = {6{and_5_out[5]}} & {P30, P30_25};  // AND_Gate and_10, 6 bits wide

  // Other names for the same wires on the sheet: P20 = BREAK; P24_20[0] = BREAK; P24_21[3:0] = P24_20;
  //   P30_25[5] = P30; X0 = IMM[0]; X11 = IMM[11]; X31 = IMM[31]; P19_12[2:0] = FUNCT3

  // Notes on the sheet:
  //   2'b11
  //   OP
  //   rd/imm
  //   funct3/imm
  //   rs1/imm
  //   rs2/imm
  //   funct7/imm
  //   contents of MicroCode (hex, n*v repeats v):
  //   40311 140001 140001 40001 40019 40015 140001 140001 40809 140001 140001 140001 60011 40019 10*140001
  //   40000 4003a 140001 4003e e0001 140001 140001 140001 40511 140001 140001 140001 3a019 140001 140001
  //   140001 41009 140001 140001 140001 7a011 11*140001 40000 7*140001 40611 140001 140001 140001 40059
  //   140001 140001 140001 41809 140001 140001 140001 60051 23*140001 400d9 7*140001 600d1 19*140001 40211
  //   140001 140001 140001 58019 7*140001 78011 11*140001 40000 7*140001 40411 140001 140001 140001 3c019
  //   7*140001 7c011 11*140001 40000 11*140001 54019 7*140001 74011 11*140001 40000 11*140001 56019
  //   7*140001 76011 11*140001 40000 7*140001 40311 140001 140001 40001 40019 40015 140001 140001 40809
  //   140001 140001 140001 62011 40019 10*140001 40000 4003a 140001 4003e 4*140001 40511 7*140001 41009
  //   15*140001 40000 7*140001 40611 140001 140001 140001 40059 140001 140001 140001 41809 27*140001 400d9
  //   27*140001 40211 140001 140001 140001 58019 19*140001 40000 7*140001 40411 140001 140001 140001 3e019
  //   7*140001 7e011 11*140001 40000 11*140001 54019 19*140001 40000 11*140001 56019 19*140001 40000
  //   7*140001 40311 140001 140001 40001 40019 40015 140001 140001 40809 140001 140001 140001 60011 40019
  //   10*140001 40000 4003a 140001 4003e e0001 140001 140001 140001 40511 140001 140001 140001 3a019
  //   140001 140001 140001 41009 140001 140001 140001 7a011 11*140001 40000 7*140001 40611 140001 140001
  //   140001 40059 140001 140001 140001 41809 140001 140001 140001 60051 23*140001 400d9 7*140001 600d1
  //   19*140001 40211 140001 140001 140001 58019 7*140001 78011 11*140001 40000 7*140001 40411 140001
  //   140001 140001 3c019 7*140001 7c011 11*140001 40000 11*140001 54019 7*140001 74011 11*140001 40000
  //   11*140001 56019 7*140001 76011 11*140001 40000 7*140001 40311 140001 140001 40001 40019 40015 140001
  //   140001 40809 140001 140001 140001 62011 40019 10*140001 40000 4003a 140001 4003e 4*140001 40511
  //   7*140001 41009 15*140001 40000 7*140001 40611 140001 140001 140001 40059 140001 140001 140001 41809
  //   27*140001 400d9 27*140001 40211 140001 140001 140001 58019 19*140001 40000 7*140001 40411 140001
  //   140001 140001 3e019 7*140001 7e011 11*140001 40000 11*140001 54019 19*140001 40000 11*140001 56019
  //   19*140001 40000 31*140001 40001 40001 140001 40001 28*140001 40001 95*140001 40001 31*140001 40001
  //   31*140001 40001 31*140001 40001 31*140001 40001 40001 140001 40001 28*140001 40001 95*140001 40001
  //   31*140001 40001 31*140001 40001 31*140001 40001 31*140001 4000e 40001 140001 40001 28*140001 4000e
  //   95*140001 4000e 31*140001 4000e 31*140001 4000e 31*140001 4000e 31*140001 4000e 40001 140001 40001
  //   28*140001 4000e 95*140001 4000e 31*140001 4000e 31*140001 4000e 31*140001 4000e 31*140001 40001
  //   31*140001 40001 95*140001 40001 31*140001 40001 31*140001 40001 31*140001 40001 31*140001 40001
  //   31*140001 40001 95*140001 40001 31*140001 40001 31*140001 40001 31*140001 40001 31*140001 40001
  //   31*140001 40001 95*140001 40001 31*140001 40001 31*140001 40001 31*140001 40001 31*140001 40001
  //   31*140001 40001 95*140001 40001 31*140001 40001 31*140001 40001 31*140001 40001 1031*140001
  //   ILL
  //   X31
  //   S[30:20]
  //   S[19:12]
  //   X11
  //   S[10:5]
  //   S[4:1].1
  //   S[4:1].0
  //   X0
endmodule

module ALU (
  input  [31:0] X,
  input  SLT,
  input  SLTU,
  input  [31:0] Y,
  input  CLK,
  input  NOP,
  input  [3:0] SEL,
  output [31:0] R
);

  wire and_2_out, and_3_out, decoder_1_out0, decoder_1_out1, decoder_1_out2, decoder_1_out3, decoder_1_out4,
       decoder_1_out5, decoder_1_out6, decoder_1_out7, decoder_1_out8, decoder_1_out9, decoder_1_out10,
       decoder_1_out11, decoder_1_out12, decoder_1_out13, decoder_1_out14, decoder_1_out15, LT, LTU,
       multiplexer_5_out, nor_1_out, not_1_out, not_2_out, or_2_out, OVF;
  wire [31:0] ANDV, bit_extender_3_out, DIFF, multiplexer_4_out, multiplexer_6_out, multiplier_1_out, ORV,
       PROD, PRODH, PRODHSU, PRODHU, QUOT, QUOTU, REMS, REMU, SARV, shifter_1_out, shifter_2_out,
       shifter_3_out, SHLV, SHRV, SUM, XORV;
  wire [32:0] bit_extender_1_out, bit_extender_2_out;
  wire [32:31] multiplier_1_cout;

  assign bit_extender_1_out = {{1{X[31]}}, X};  // Bit_Extender bit_extender_1
  assign bit_extender_2_out = {{1{1'b0}}, Y};  // Bit_Extender bit_extender_2
  Multiplier #(.mode("twosComplement"), .width(33)) multiplier_1 (
    .a(bit_extender_1_out), .b(bit_extender_2_out), .out({PRODHSU[0], multiplier_1_out}),
    .cout({multiplier_1_cout, PRODHSU[31:1]}));  // open: cin
  Adder #(.width(32)) adder_1 (.a(X), .b(Y), .out(SUM));  // open: cin, cout
  Subtractor #(.width(32)) subtractor_1 (.a(X), .b(Y), .out(DIFF));  // open: bin, bout
  Multiplier #(.mode("twosComplement"), .width(32)) multiplier_2 (.a(X), .b(Y), .out(PROD), .cout(PRODH));  // open: cin
  Multiplier #(.width(32)) multiplier_3 (.a(X), .b(Y), .cout(PRODHU));  // open: out, cin
  Divider #(.mode("twosComplement"), .width(32)) divider_1 (.a(X), .b(Y), .out(QUOT), .rem(REMS));  // open: upper
  Divider #(.width(32)) divider_2 (.a(X), .b(Y), .out(QUOTU), .rem(REMU));  // open: upper
  Register #(.trigger("high"), .width(32)) u_SUM (.D(SUM), .clk(1'b1));  // open: en, Q, clr
  Register #(.trigger("high"), .width(32)) u_DIFF (.D(DIFF), .clk(1'b1));  // open: en, Q, clr
  Register #(.trigger("high"), .width(32)) u_PROD (.D(PROD), .clk(1'b1));  // open: en, Q, clr
  Register #(.trigger("high"), .width(32)) u_PRODH (.D(PRODH), .clk(1'b1));  // open: en, Q, clr
  Register #(.trigger("high"), .width(32)) u_PRODHU (.D(PRODHU), .clk(1'b1));  // open: en, Q, clr
  Register #(.trigger("high"), .width(32)) u_PRODHSU (.D(PRODHSU), .clk(1'b1));  // open: en, Q, clr
  Register #(.trigger("high"), .width(32)) u_QUOT (.D(QUOT), .clk(1'b1));  // open: en, Q, clr
  Register #(.trigger("high"), .width(32)) u_REMS (.D(REMS), .clk(1'b1));  // open: en, Q, clr
  Register #(.trigger("high"), .width(32)) u_QUOTU (.D(QUOTU), .clk(1'b1));  // open: en, Q, clr
  Register #(.trigger("high"), .width(32)) u_REMU (.D(REMU), .clk(1'b1));  // open: en, Q, clr
  assign ORV = X | Y;  // OR_Gate or_1, 32 bits wide
  assign ANDV = X & Y;  // AND_Gate and_1, 32 bits wide
  assign XORV = X ^ Y;  // XOR_Gate xor_1, 32 bits wide
  Shifter #(.width(32)) shifter_1 (.in(X), .\dist (Y[4:0]), .out(shifter_1_out));
  Shifter #(.shift("lr"), .width(32)) shifter_2 (.in(X), .\dist (Y[4:0]), .out(shifter_2_out));
  Shifter #(.shift("ar"), .width(32)) shifter_3 (.in(X), .\dist (Y[4:0]), .out(shifter_3_out));
  Comparator #(.width(32)) comparator_1 (.a(X), .b(Y), .lt(LT));  // open: gt, eq
  Comparator #(.mode("unsigned"), .width(32)) comparator_2 (.a(X), .b(Y), .lt(LTU));  // open: gt, eq
  Multiplexer #(.width(32)) multiplexer_1 (.in0(shifter_1_out), .in1({32{1'b0}}), .out(SHLV), .sel(OVF));
  Multiplexer #(.width(32)) multiplexer_2 (.in0(shifter_2_out), .in1({32{1'b0}}), .out(SHRV), .sel(OVF));
  Multiplexer #(.width(32)) multiplexer_3 (.in0(shifter_3_out), .in1({32{1'b0}}), .out(SARV), .sel(OVF));
  Register #(.trigger("high"), .width(32)) u_ORV (.D(ORV), .clk(1'b1));  // open: en, Q, clr
  Register #(.trigger("high"), .width(32)) u_ANDV (.D(ANDV), .clk(1'b1));  // open: en, Q, clr
  Register #(.trigger("high"), .width(32)) u_XORV (.D(XORV), .clk(1'b1));  // open: en, Q, clr
  Register #(.trigger("high"), .width(32)) u_SHLV (.D(SHLV), .clk(1'b1));  // open: en, Q, clr
  Register #(.trigger("high"), .width(32)) u_SHRV (.D(SHRV), .clk(1'b1));  // open: en, Q, clr
  Register #(.trigger("high"), .width(32)) u_SARV (.D(SARV), .clk(1'b1));  // open: en, Q, clr
  LED F_SUM (.in(decoder_1_out0));
  LED F_DIFF (.in(decoder_1_out1));
  LED F_PROD (.in(decoder_1_out2));
  LED F_PRODH (.in(decoder_1_out3));
  LED F_PRODHU (.in(decoder_1_out4));
  LED F_PRODHSU (.in(decoder_1_out5));
  LED F_QUOT (.in(decoder_1_out6));
  LED F_REMS (.in(decoder_1_out7));
  LED F_QUOTU (.in(decoder_1_out8));
  LED F_REMU (.in(decoder_1_out9));
  LED F_ORV (.in(decoder_1_out10));
  LED F_ANDV (.in(decoder_1_out11));
  LED F_XORV (.in(decoder_1_out12));
  LED F_SHLV (.in(decoder_1_out13));
  LED F_SHRV (.in(decoder_1_out14));
  LED F_SARV (.in(decoder_1_out15));
  Multiplexer #(.select(4), .width(32)) multiplexer_4 (
    .in0(SUM), .in1(DIFF), .in2(PROD), .in3(PRODH), .in4(PRODHU), .in5(PRODHSU), .in6(QUOT), .in7(REMS),
    .in8(QUOTU), .in9(REMU), .in10(ORV), .in11(ANDV), .in12(XORV), .in13(SHLV), .in14(SHRV), .in15(SARV),
    .out(multiplexer_4_out), .sel(SEL));
  Decoder #(.select(4)) decoder_1 (
    .out0(decoder_1_out0), .out1(decoder_1_out1), .out2(decoder_1_out2), .out3(decoder_1_out3),
    .out4(decoder_1_out4), .out5(decoder_1_out5), .out6(decoder_1_out6), .out7(decoder_1_out7),
    .out8(decoder_1_out8), .out9(decoder_1_out9), .out10(decoder_1_out10), .out11(decoder_1_out11),
    .out12(decoder_1_out12), .out13(decoder_1_out13), .out14(decoder_1_out14), .out15(decoder_1_out15),
    .sel(SEL), .en(nor_1_out));
  nor nor_1 (nor_1_out, SLT, SLTU);
  Multiplexer multiplexer_5 (.in0(LT), .in1(LTU), .out(multiplexer_5_out), .sel(SLTU));
  Multiplexer #(.width(32)) multiplexer_6 (
    .in0(multiplexer_4_out), .in1(bit_extender_3_out), .out(multiplexer_6_out), .sel(SLT));
  assign bit_extender_3_out = {{31{1'b0}}, multiplexer_5_out};  // Bit_Extender bit_extender_3
  or or_2 (or_2_out, not_1_out, NOP);
  not not_1 (not_1_out, CLK);
  Register #(.trigger("high"), .width(32)) VX (.D(X), .clk(1'b1));  // open: en, Q, clr
  LED C_LT (.in(LT));
  LED C_LTU (.in(LTU));
  Register #(.width(32)) VR (.D(multiplexer_6_out), .clk(or_2_out), .Q(R));  // open: en, clr
  and and_2 (and_2_out, SLT, not_2_out);
  not not_2 (not_2_out, SLTU);
  and and_3 (and_3_out, SLT, SLTU);
  Register #(.trigger("high"), .width(32)) VY (.D(Y), .clk(1'b1));  // open: en, Q, clr
  LED V_SLT (.in(and_2_out));
  LED V_SLTU (.in(and_3_out));
  or or_3 (OVF, Y[5], Y[6], Y[7], Y[8], Y[9], Y[10], Y[11], Y[12], Y[13], Y[14], Y[15], Y[16], Y[17], Y[18], Y[19], Y[20], Y[21], Y[22], Y[23], Y[24], Y[25], Y[26], Y[27], Y[28], Y[29], Y[30], Y[31]);

  // Other names for the same wires on the sheet: Y4_0[4:0] = Y[4:0]
endmodule

module BusInterface (
  input  LOAD0,
  input  LOAD1,
  input  [31:0] DI,
  input  STORE0,
  input  STORE1,
  input  LDSX,
  input  LD,
  input  CLK,
  input  RST,
  input  nBUSY,
  input  [31:0] ADDR,
  input  [31:0] DOUT,
  output EALIGN,
  output BM0,
  output BM1,
  output [31:0] DIN,
  output BM2,
  output BM3,
  output nRW,
  output STROBE,
  output RDY,
  output [29:0] A,
  output [31:0] DO
);

  wire A0, A1, and_9_out, and_10_out, IO, LB, M0, M1, M2, M3, nand_1_out, not_1_out, not_2_out, ST;
  wire [6:0] bit_extender_9_out, multiplexer_6_out;
  wire [6:6] MaskGen_p3;
  wire [7:0] and_1_out, and_2_out, and_3_out, and_4_out, and_5_out, and_6_out, and_7_out, and_8_out,
       bit_extender_1_out, bit_extender_2_out, bit_extender_3_out, bit_extender_4_out, bit_extender_5_out,
       bit_extender_6_out, bit_extender_7_out, bit_extender_8_out;
  wire [15:0] bit_extender_10_out, multiplexer_7_out;
  wire [15:15] multiplexer_5_out;
  wire [31:0] MDO_q, multiplexer_1_out, multiplexer_2_out, multiplexer_3_out, multiplexer_4_out,
       shifter_1_out, shifter_2_out, shifter_3_out, shifter_4_out;

  Shifter #(.width(32)) shifter_1 (.in(DOUT), .\dist (5'b01000), .out(shifter_1_out));
  assign bit_extender_1_out = {{7{M0}}, M0};  // Bit_Extender bit_extender_1
  assign bit_extender_2_out = {{7{M1}}, M1};  // Bit_Extender bit_extender_2
  assign bit_extender_3_out = {{7{M2}}, M2};  // Bit_Extender bit_extender_3
  assign bit_extender_4_out = {{7{M3}}, M3};  // Bit_Extender bit_extender_4
  Multiplexer #(.width(32)) multiplexer_1 (.in0(DOUT), .in1(shifter_1_out), .out(multiplexer_1_out), .sel(A0));
  assign and_1_out = DI[7:0] & bit_extender_1_out;  // AND_Gate and_1, 8 bits wide
  assign and_2_out = DI[15:8] & bit_extender_2_out;  // AND_Gate and_2, 8 bits wide
  assign and_3_out = DI[23:16] & bit_extender_3_out;  // AND_Gate and_3, 8 bits wide
  assign and_4_out = DI[31:24] & bit_extender_4_out;  // AND_Gate and_4, 8 bits wide
  Multiplexer #(.width(32)) multiplexer_2 (
    .in0(multiplexer_1_out), .in1(shifter_2_out), .out(multiplexer_2_out), .sel(A1));
  Shifter #(.width(32)) shifter_2 (.in(multiplexer_1_out), .\dist (5'b10000), .out(shifter_2_out));
  Shifter #(.shift("lr"), .width(32)) shifter_3 (
    .in({and_4_out, and_3_out, and_2_out, and_1_out}), .\dist (5'b01000), .out(shifter_3_out));
  Multiplexer #(.width(32)) multiplexer_3 (
    .in0({and_4_out, and_3_out, and_2_out, and_1_out}), .in1(shifter_3_out), .out(multiplexer_3_out), .sel(A0));
  Shifter #(.shift("lr"), .width(32)) shifter_4 (.in(multiplexer_3_out), .\dist (5'b10000), .out(shifter_4_out));
  assign and_5_out = multiplexer_2_out[7:0] & bit_extender_5_out;  // AND_Gate and_5, 8 bits wide
  assign bit_extender_5_out = {{7{M0}}, M0};  // Bit_Extender bit_extender_5
  assign and_6_out = multiplexer_2_out[15:8] & bit_extender_6_out;  // AND_Gate and_6, 8 bits wide
  assign bit_extender_6_out = {{7{M1}}, M1};  // Bit_Extender bit_extender_6
  assign and_7_out = multiplexer_2_out[23:16] & bit_extender_7_out;  // AND_Gate and_7, 8 bits wide
  assign bit_extender_7_out = {{7{M2}}, M2};  // Bit_Extender bit_extender_7
  assign and_8_out = multiplexer_2_out[31:24] & bit_extender_8_out;  // AND_Gate and_8, 8 bits wide
  assign bit_extender_8_out = {{7{M3}}, M3};  // Bit_Extender bit_extender_8
  Multiplexer #(.width(32)) multiplexer_4 (
    .in0(multiplexer_3_out), .in1(shifter_4_out), .out(multiplexer_4_out), .sel(A1));
  Register #(.width(32)) MDO (
    .D({and_8_out, and_7_out, and_6_out, and_5_out}), .clk(and_9_out), .Q(MDO_q));  // open: en, clr
  and and_9 (and_9_out, IO, ST);
  Multiplexer multiplexer_5 (
    .in0(multiplexer_4_out[15]), .in1(multiplexer_4_out[7]), .out(multiplexer_5_out[15]), .sel(and_10_out));
  and and_10 (and_10_out, LB, LDSX);
  assign DO = nRW ? MDO_q : 32'bz;  // Controlled_Buffer controlled_buffer_1
  assign bit_extender_9_out = {{6{multiplexer_4_out[7]}}, multiplexer_4_out[7]};  // Bit_Extender bit_extender_9
  assign bit_extender_10_out = {{15{multiplexer_5_out[15]}}, multiplexer_5_out[15]};  // Bit_Extender bit_extender_10
  Multiplexer #(.width(7)) multiplexer_6 (
    .in0(multiplexer_4_out[14:8]), .in1(bit_extender_9_out), .out(multiplexer_6_out), .sel(and_10_out));
  Register #(.width(32)) MDI (
    .D({multiplexer_7_out, multiplexer_5_out[15], multiplexer_6_out, multiplexer_4_out[7:0]}),
    .clk(nand_1_out), .Q(DIN));  // open: en, clr
  Multiplexer #(.width(16)) multiplexer_7 (
    .in0(multiplexer_4_out[31:16]), .in1(bit_extender_10_out), .out(multiplexer_7_out), .sel(LDSX));
  nand nand_1 (nand_1_out, IO, nBUSY);
  D_Flip_Flop d_ff_1 (.D(nBUSY), .clk(not_1_out), .Q(RDY), .preset(RST));  // open: Qn, reset
  not not_1 (not_1_out, IO);
  and and_11 (STROBE, IO, not_2_out);
  not not_2 (not_2_out, RST);
  Register #(.width(32)) MAR (.D(ADDR), .clk(IO), .Q({A, A1, A0}));  // open: en, clr
  // PlaRom #(.Contents("0*4 1 2 0 0 1 0 1 2 1 1 0 0 2 0*3 1 2 1 0 1 1 2 0*4 1 0 1 2 1 0 1 2 1 0 1 0*3 2 0*4 2 0*3 1 1 0 0 2 2 1 1 2 0 0 2 1 1 0 2 2 0 1 1 2 2 0 0 2 2 1 0 1 2*3 1 2 1 0 2 1 0 1 2 1 2 1 2 1 0 1 2 1 1 0 1 2 2 1 1 2 1 0 1 2 1 0 1 2 1 2 1 2 1 0 1 1 0*3 2 1 1 0 2 0*3 2 0 0 2 0 0 2 2 0*3 2 0*3 2*3 0 2 0 0 2 2 0 0 2 2 0 2 0 2 2 0 0 1 0*8 1 0*7 1 0*3 1 1 0 0 1 0*7 1 0*3 1 1 0 0 1 0*7 1 0*8 1 0*7 1 0*8 1 1 0*6 1 1 0*6 1 1 0*6 1 1 0*6 1 0*7 1 0*7 1 1 0*6 1 1 0*7 1 0*7 1 0*8 1 0*7 1 0*8 1 0*7 1 0*8 1 0*7 1 0*7 1 0*7 1 0*7 1 0*7 1"), .\and (29), .outputs(8)) MaskGen: pin names not known; wires that end beside it: {A1, A0, STORE1, STORE0, LOAD1, LOAD0}, 1'b0, {LB, MaskGen_p3[6], ST, M3, M2, M1, M0, EALIGN}
  Register #(.width(5)) register_1 (
    .D({ST, M3, M2, M1, M0}), .clk(IO), .Q({nRW, BM3, BM2, BM1, BM0}));  // open: en, clr
  and and_12 (IO, MaskGen_p3[6], CLK);

  // Other names for the same wires on the sheet: OE = nRW

  // Notes on the sheet:
  //   LD: pull=up
  //   RST: pull=up
  //   nBUSY: pull=up
endmodule

module FetchUnit (
  input  [31:0] IPC,
  input  [31:0] EMA,
  input  [31:0] DIN,
  input  BUS_RDY,
  input  SX,
  input  LD0,
  input  ILL_IN,
  input  LD1,
  input  NOP,
  input  ST0,
  input  ST1,
  input  RST,
  input  FETCH,
  input  IO,
  input  CLK,
  output [31:0] NPC,
  output [31:0] PC,
  output [31:0] ADDR,
  output ID,
  output [31:0] TAP,
  output [31:0] INSTR,
  output PCE,
  output LDSX,
  output ILL,
  output LOAD0,
  output LOAD1,
  output LOAD,
  output STORE0,
  output STORE1
);

  wire and_1_out, and_5_out, CLK_t, d_ff_1_q, d_ff_2_q, d_ff_4_q, d_ff_5_q, NOP_t, not_1_out, not_2_out,
       not_3_out, not_4_out, not_5_out, not_6_out, not_7_out, not_8_out, or_1_out, or_2_out, or_4_out,
       or_5_out;
  wire [31:0] IDR_q, multiplexer_4_out, register_1_q, register_3_q;

  or or_1 (or_1_out, ST1, ST0);
  not not_1 (not_1_out, IO);
  Multiplexer #(.width(32)) multiplexer_1 (.in0(IPC), .in1(EMA), .out(ADDR), .sel(or_2_out));
  or or_2 (or_2_out, or_1_out, LOAD, not_2_out);
  or or_3 (LOAD, LD1, LD0);
  not not_2 (not_2_out, BUS_RDY);
  and and_1 (and_1_out, FETCH, not_1_out);
  not not_3 (not_3_out, or_2_out);
  and and_2 (ID, not_3_out, and_1_out);
  and and_3 (PCE, and_1_out, BUS_RDY);
  and and_4 (LDSX, LOAD, SX);
  Multiplexer multiplexer_2 (.in0(and_1_out), .in1(LD0), .out(LOAD0), .sel(LOAD));
  Multiplexer multiplexer_3 (.in0(and_1_out), .in1(LD1), .out(LOAD1), .sel(LOAD));
  LED FETCHING (.in(ID));
  Register #(.width(32)) register_1 (.D(IPC), .clk(and_5_out), .Q(register_1_q));  // open: en, clr
  and and_5 (and_5_out, PCE, CLK_t);
  Register #(.width(32)) register_2 (.D(register_1_q), .clk(not_4_out), .Q(NPC));  // open: en, clr
  not not_4 (not_4_out, and_5_out);
  Register #(.width(32)) register_3 (.D(NPC), .clk(and_5_out), .Q(register_3_q));  // open: en, clr
  not not_5 (not_5_out, and_5_out);
  Multiplexer #(.width(32)) multiplexer_4 (.in0(DIN), .in1(32'h13), .out(multiplexer_4_out), .sel(NOP_t));
  and and_6 (CLK_t, not_6_out, CLK);
  not not_6 (not_6_out, NOP);
  Register #(.width(32)) register_4 (.D(register_3_q), .clk(not_5_out), .Q(PC));  // open: en, clr
  Register #(.width(32)) register_5 (.D(multiplexer_4_out), .clk(CLK_t), .Q(TAP));  // open: en, clr
  not not_7 (not_7_out, CLK_t);
  D_Flip_Flop d_ff_1 (.D(NOP), .clk(CLK), .Q(d_ff_1_q));  // open: Qn, preset, reset
  D_Flip_Flop d_ff_2 (.D(RST), .clk(CLK), .Q(d_ff_2_q));  // open: Qn, preset, reset
  Register #(.width(32)) IDR (.D(TAP), .clk(not_7_out), .Q(IDR_q));  // open: en, clr
  not not_8 (not_8_out, CLK);
  D_Flip_Flop d_ff_3 (.D(d_ff_1_q), .clk(not_8_out), .Q(NOP_t));  // open: Qn, preset, reset
  D_Flip_Flop d_ff_4 (.D(d_ff_2_q), .clk(not_8_out), .Q(d_ff_4_q));  // open: Qn, preset, reset
  or or_4 (or_4_out, ILL_IN, or_5_out);
  or or_5 (or_5_out, RST, d_ff_2_q, d_ff_4_q, d_ff_5_q);
  D_Flip_Flop d_ff_5 (.D(d_ff_4_q), .clk(CLK), .Q(d_ff_5_q));  // open: Qn, preset, reset
  Multiplexer #(.width(32)) multiplexer_5 (.in0(IDR_q), .in1(32'h13), .out(INSTR), .sel(or_4_out));

  assign ILL = ILL_IN;
  assign STORE0 = ST0;
  assign STORE1 = ST1;
endmodule

module InstructionValidator (
  input  [31:0] INSTR,
  input  ID,
  output ILL
);

  wire and_1_out, and_2_out, FUNCT, nand_1_out, or_1_out, or_2_out, or_3_out, SYS;
  wire [0:0] CHK_p3;
  wire [6:0] CLF_p3;

  nand nand_1 (nand_1_out, INSTR[0], INSTR[1]);
  // PlaRom #(.Contents("1 2 2 1 1 2 2 1 1 2*4 1*4 0 1*5 2 2 1 2 1*3 2 2 1*4 0 2 1 2*3 1 2 2 0 0 2 2 0*4 2 1 2 1 0*3 2 0 2 0 2 1 2 1 0 2 1 0 1 1 2 1 0*7 1 0*6 1 0*6 1 0*6 1 0*7 1 0*7 1 0*7 1 0*7 1 0*7 1 0*6 1 0*6 1 0*6 1 0*6 1 0*6 1"), .\and (15), .outputs(7)) CLF: pin names not known; wires that end beside it: INSTR[6:2], 1'b0, CLF_p3
  // PlaRom #(.Contents("1 0*4 1 2 2 1 1 0 1 2 1 2 1 0 2 1*4 0 1 2 1 0 2 1*7 0 2 2 1 1 0 1*5 2 2 1*7 2*3 1 1 0*7 2 2 0*9 2 1 0*5 2 1 0*7 2 2 0 2 0*4 2 0 0 2 0 2 0*7 2 0 2 0 2 0 2 0*3 2 0 2 0 0 2 0*4 2 0 2 0*6 2 0 1 0 2 0*4 2 0 0 1 0 2 0*3 2 0*3 1 0 2 0*4 2 2 1 0 1 0*6 2 0 0 1 1 2 0 0 2 2 0 0 1 1 0*4 1 2 0 2 0 0 1 0*3 2 0*4 1 1 2 0 0 2 0 0 1 2 1 0*7 1 2 1 0 2 2 0 0 2 0 0 2 2 0 1 2 2 0*4 2 2 0 1 0*5 1 0 1 1 2 0 2 0 1 2 0 1 2 0 1 2 0 1 1 2 0 0 2 0 1 2 0 2 0 1 1 2 0 0 1 1 0 0 1 0 0 1 0 0 1 0 0 1 0*3 1 0*3 1 0 0 1 0 0 1 0 0 1 0 0 1 0 0 1 0 0 1 0 0 1 0 0 1 0 0 1 0 0 1 0 0 1 0 0 1 0 0 1 0 0 1 0 0 1 0 0 1 0 0 1 0 0 1 0 0 1 0 0 1 0 0 1 0 0 1 0 0 1"), .\and (30), .outputs(3)) CHK: pin names not known; wires that end beside it: {INSTR[30], INSTR[25], INSTR[14:12], INSTR[6:2]}, 1'b0, {FUNCT, SYS, CHK_p3[0]}
  LED R (.in(CLF_p3[6]));
  or or_1 (or_1_out, INSTR[21], INSTR[22], INSTR[23], INSTR[24]);
  or or_2 (or_2_out, INSTR[31], INSTR[26], INSTR[27], INSTR[28], INSTR[29]);
  LED I (.in(CLF_p3[5]));
  LED S (.in(CLF_p3[4]));
  LED B (.in(CLF_p3[3]));
  LED U (.in(CLF_p3[2]));
  and and_1 (and_1_out, SYS, or_1_out);
  and and_2 (and_2_out, FUNCT, or_2_out);
  LED J (.in(CLF_p3[1]));
  or or_3 (or_3_out, and_1_out, and_2_out, nand_1_out, CLF_p3[0], CHK_p3[0]);
  and and_3 (ILL, or_3_out, ID);

  // Other names for the same wires on the sheet: P24_21[3:0] = INSTR[24:21]; P29_26[3:0] = INSTR[29:26];
  //   P31 = INSTR[31]

  // Notes on the sheet:
  //   1'b1
  //   1'b1
  //   OP [6:2]
  //   funct3/imm [14:12]
  //   rs2/imm [24:21]
  //   funct7/imm [25]
  //   funct7/imm [29:26]
  //   funct7/imm [30]
  //   funct7/imm [31]
endmodule

module RegisterDecoder (
  input  [31:0] INSTR,
  output [4:0] RD,
  output [4:0] RS1,
  output [4:0] RS2
);

  wire DE, S1E, S2E;

  // PlaRom #(.Contents("0 2 0 1*3 0 0 1 1 2 2 1 1 0 1*3 2 2 0 2 1*4 2 0 1*3 0 2 1 0 2 2 1 0 2 0 2 2 1*4 0 1 1 1 0 0 1 0 0 1 0 0 1 0 1 0 1 0 0 1 0*3 1 0 0 1 0 0 1 0 0 1"), .\and (10), .outputs(3)) MASK: pin names not known; wires that end beside it: INSTR[6:2], 1'b0, {S1E, S2E, DE}
  assign RD = {5{DE}} & INSTR[11:7];  // AND_Gate and_1, 5 bits wide
  assign RS1 = {5{S1E}} & INSTR[19:15];  // AND_Gate and_2, 5 bits wide
  assign RS2 = {5{S2E}} & INSTR[24:20];  // AND_Gate and_3, 5 bits wide
  Register #(.trigger("high"), .width(5)) V_RD (.D(RD), .clk(1'b1));  // open: en, Q, clr
  Register #(.trigger("high"), .width(5)) V_RS1 (.D(RS1), .clk(1'b1));  // open: en, Q, clr
  Register #(.trigger("high"), .width(5)) V_RS2 (.D(RS2), .clk(1'b1));  // open: en, Q, clr

  // Notes on the sheet:
  //   OP[6:2]
  //   rd[11:7]
  //   rs1[19:15]
  //   rs2[24:20]
endmodule

module ArithmeticDecoder (
  input  [31:0] INSTR,
  output [31:0] IMM,
  output PCREL,
  output OPIMM,
  output SLT,
  output SLTU,
  output [3:0] ALU_OP
);

  wire nSHIFT, S4_1_0, S4_1_1, S10_5, S19_12, S30_20;
  wire [3:0] and_2_out, and_3_out;
  wire [5:5] and_1_out;

  // Probe on INSTR[6:2]
  // Probe on INSTR[11:7]
  // Probe on INSTR[14:12]
  // Probe on INSTR[19:15]
  // Probe on INSTR[24:20]
  // Probe on INSTR[31:25]
  // PlaRom #(.Contents("0 0 2 1 2 1*3 0 2 0 2*3 1 1 0 2 0 2 2 1 1 2 0 2 0 1*3 2 2 0 2 0 1 1 0 1 1 0*3 2*3 1 1 0*3 2 2 1 0 2 0*3 1*3 2 2 0*3 1 1 0 1 1 0*4 2 1*3 0*3 2 0*8 1 0 0 1 0*5 1 0*8 2 0*3 2*3 1*3 0 2 0 2 2 1 2*3 0 0 2 0*4 2 0*3 1 0 0 1 2 0*4 1 0 0 2 0*5 2 0*4 1 0 2 1 2 0*3 2 2 1 2*3 0*3 1 0*3 2 0*6 2 1 0*7 1 0*7 1 0*7 1 0*7 1 0*8 1 0*7 1 0*7 1 0*7 1 0*8 1 0*8 1 0*7 1 0*7 1 0*7 1 0*8 1 0*7 1 0*7 1 0 0 1 0*4 1 0*7 1 0 0 1 0*4 1 0 0 1 0*5 1 1 0*6 1 0*9 1 0*7 1"), .\and (24), .outputs(8)) IDEC: pin names not known; wires that end beside it: {INSTR[31], INSTR[20], INSTR[7:2]}, 1'b0, {IMM[0], S4_1_0, S4_1_1, S10_5, IMM[11], S19_12, S30_20, IMM[31]}
  ROM #(.addrWidth(10), .dataWidth(9)) rom_1 (
    .addr({INSTR[30], INSTR[25], INSTR[14:12], INSTR[6:2]}), .data({nSHIFT, ALU_OP, SLTU, SLT, OPIMM, PCREL}));
  and and_1 (and_1_out[5], S10_5, nSHIFT);
  assign and_2_out = {4{S4_1_1}} & INSTR[11:8];  // AND_Gate and_2, 4 bits wide
  assign IMM[4:1] = and_2_out | and_3_out;  // OR_Gate or_1, 4 bits wide
  assign and_3_out = {4{S4_1_0}} & INSTR[24:21];  // AND_Gate and_3, 4 bits wide
  assign IMM[10:5] = {6{and_1_out[5]}} & INSTR[30:25];  // AND_Gate and_4, 6 bits wide
  Multiplexer #(.width(8)) multiplexer_1 (.in0({8{IMM[31]}}), .in1(INSTR[19:12]), .out(IMM[19:12]), .sel(S19_12));
  Multiplexer #(.width(11)) multiplexer_2 (.in0({11{IMM[31]}}), .in1(INSTR[30:20]), .out(IMM[30:20]), .sel(S30_20));
  Register #(.trigger("high"), .width(32)) register_1 (.D(IMM), .clk(1'b1));  // open: en, Q, clr

  // Other names for the same wires on the sheet: OP[4:0] = INSTR[6:2]; FUNCT3[2:0] = INSTR[14:12];
  //   P19_12[7:0] = INSTR[19:12]; P7 = INSTR[7]; P31 = INSTR[31]; P20 = INSTR[20]; P24_20[4:0] = INSTR[24:20];
  //   P24_21[3:0] = INSTR[24:21]; P25 = INSTR[25]; P30_25[5:0] = INSTR[30:25]; P30 = INSTR[30]; X0 = IMM[0];
  //   X11 = IMM[11]; X31 = IMM[31]; P11_8[3:0] = INSTR[11:8]

  // Notes on the sheet:
  //   OP [6:2]
  //   rd/imm [11:7]
  //   funct3/imm [14:12]
  //   rs1/imm [19:15]
  //   rs2/imm [24:20]
  //   funct7/imm [31:25]
  //   contents of rom_1 (hex, n*v repeats v):
  //   102 100 100 100 102 103 100 100 102 4*100 102 10*100 103 102 100 103 4*100 102 100 100 100 d2 103
  //   100 100 102 100 100 100 1d0 102 10*100 103 100 100 103 4*100 102 100 100 100 106 103 100 100 102 100
  //   100 100 104 102 13*100 103 8*100 10e 103 6*100 10c 102 13*100 103 4*100 102 100 100 100 1c2 103
  //   6*100 1c0 102 10*100 103 100 100 103 4*100 102 100 100 100 e2 103 6*100 1e0 102 10*100 103 100 100
  //   103 8*100 1a2 103 6*100 1a0 102 10*100 103 100 100 103 8*100 1b2 103 6*100 1b0 102 10*100 103 100
  //   100 103 4*100 102 100 100 100 102 103 100 100 102 100 100 100 120 102 10*100 103 102 100 103 4*100
  //   102 4*100 103 100 100 102 100 100 100 130 102 10*100 103 100 100 103 4*100 102 100 100 100 106 103
  //   100 100 102 100 100 100 150 102 13*100 103 8*100 10e 103 6*100 140 102 13*100 103 4*100 102 100 100
  //   100 1c2 103 6*100 160 102 10*100 103 100 100 103 4*100 102 4*100 103 6*100 170 102 10*100 103 100
  //   100 103 8*100 1a2 103 6*100 180 102 10*100 103 100 100 103 8*100 1b2 103 6*100 190 102 10*100 103
  //   100 100 103 4*100 102 100 100 100 102 103 100 100 102 100 100 100 110 102 10*100 103 102 100 103
  //   4*100 102 4*100 103 100 100 102 4*100 102 10*100 103 100 100 103 4*100 102 100 100 100 106 103 100
  //   100 102 4*100 102 13*100 103 8*100 10e 103 7*100 102 13*100 103 4*100 102 100 100 100 1c2 103 7*100
  //   102 10*100 103 100 100 103 4*100 102 100 100 100 f2 103 6*100 1f0 102 10*100 103 100 100 103 8*100
  //   1a2 103 7*100 102 10*100 103 100 100 103 8*100 1b2 103 7*100 102 10*100 103 100 100 103 4*100 102
  //   100 100 100 102 103 100 100 102 4*100 102 10*100 103 102 100 103 4*100 102 4*100 103 100 100 102
  //   4*100 102 10*100 103 100 100 103 4*100 102 100 100 100 106 103 100 100 102 4*100 102 13*100 103
  //   8*100 10e 103 7*100 102 13*100 103 4*100 102 100 100 100 1c2 103 7*100 102 10*100 103 100 100 103
  //   4*100 102 4*100 103 7*100 102 10*100 103 100 100 103 8*100 1a2 103 7*100 102 10*100 103 100 100 103
  //   8*100 1b2 103 7*100 102 10*100 103 100 100 103 4*100
  //   X31
  //   S[30:20]
  //   S[19:12]
  //   X11
  //   S[10:5]
  //   S[4:1].1
  //   S[4:1].0
  //   X0
endmodule

module LoadStoreUnit (
  input  [31:0] INSTR,
  input  CLK,
  input  RDY,
  input  RST,
  output ST0,
  output ST1,
  output LD1,
  output SX,
  output LD0,
  output NOP,
  output IOE
);

  wire nor_2_out, not_1_out, not_2_out, not_3_out, not_4_out, or_1_out, or_2_out, or_3_out, t_ff_1_q,
       t_ff_1_qn;
  wire [4:0] register_1_q;

  nor nor_1 (IOE, INSTR[2], INSTR[3], INSTR[4], INSTR[6]);
  Register #(.width(5)) register_1 (
    .D({IOE, INSTR[14:12], INSTR[5]}), .clk(not_1_out), .Q(register_1_q));  // open: en, clr
  not not_1 (not_1_out, CLK);
  T_Flip_Flop t_ff_1 (.T(or_1_out), .clk(not_1_out), .Q(t_ff_1_q), .Qn(t_ff_1_qn), .reset(or_2_out));  // open: preset
  or or_1 (or_1_out, RDY, t_ff_1_qn);
  or or_2 (or_2_out, not_2_out, RST);
  not not_2 (not_2_out, IOE);
  not not_3 (not_3_out, register_1_q[1]);
  not not_4 (not_4_out, register_1_q[0]);
  or or_3 (or_3_out, register_1_q[1], register_1_q[2]);
  nor nor_2 (nor_2_out, register_1_q[2], register_1_q[3]);
  and and_1 (ST0, not_3_out, t_ff_1_q, register_1_q[0]);
  and and_2 (ST1, register_1_q[0], t_ff_1_q, or_3_out);
  and and_3 (LD1, not_4_out, t_ff_1_q, or_3_out);
  and and_4 (SX, not_4_out, t_ff_1_q, nor_2_out);
  and and_5 (LD0, not_4_out, t_ff_1_q, not_3_out);
  and and_6 (NOP, register_1_q[4], t_ff_1_q);

  // Notes on the sheet:
  //   OP [5]
  //   funct3/imm [12]
  //   funct3/imm [13]
  //   funct3/imm [14]
  //   OP [2]
  //   OP [3]
  //   OP [4]
  //   OP [6]
endmodule

module StageBuffer (
  input  [31:0] PC_IN,
  input  [31:0] NPC_IN,
  input  SUP,
  input  [31:0] INSTR_IN,
  input  CLK,
  input  NOP,
  input  NOP_IN,
  output [31:0] PC,
  output [31:0] PC_OUT,
  output [31:0] NPC_OUT,
  output [31:0] INSTR,
  output [31:0] INSTR_OUT,
  output NOP_OUT
);

  wire and_1_out, not_1_out, not_2_out;
  wire [31:0] ISR_q, multiplexer_2_out, NPR_q;

  not not_1 (not_1_out, NOP_OUT);
  or or_1 (NOP_OUT, NOP, NOP_IN);
  Register #(.width(32)) PCR (.D(PC_IN), .clk(and_1_out), .Q(PC));  // open: en, clr
  Register #(.width(32)) NPR (.D(NPC_IN), .clk(and_1_out), .Q(NPR_q));  // open: en, clr
  Register #(.width(32)) ISR (.D(INSTR_IN), .clk(and_1_out), .Q(ISR_q));  // open: en, clr
  and and_1 (and_1_out, CLK, not_1_out);
  Register #(.width(32)) register_1 (.D(PC), .clk(not_2_out), .Q(PC_OUT));  // open: en, clr
  Register #(.width(32)) register_2 (.D(NPR_q), .clk(not_2_out), .Q(NPC_OUT));  // open: en, clr
  not not_2 (not_2_out, and_1_out);
  Multiplexer #(.width(32)) multiplexer_1 (.in0(ISR_q), .in1(32'h13), .out(INSTR), .sel(SUP));
  Register #(.width(32)) register_3 (.D(multiplexer_2_out), .clk(not_2_out), .Q(INSTR_OUT));  // open: en, clr
  Multiplexer #(.width(32)) multiplexer_2 (.in0(INSTR), .in1(32'h13), .out(multiplexer_2_out), .sel(NOP_OUT));
endmodule

module ResultBuffer (
  input  [31:0] V_IN,
  input  [31:0] D_IN,
  input  LD,
  input  [31:0] X_IN,
  input  [31:0] Y_IN,
  input  CLK,
  input  NOP,
  output [31:0] Y,
  output [31:0] VAL,
  output EQ,
  output LT,
  output LTU
);

  wire and_1_out, comparator_1_eq, comparator_1_lt, comparator_2_lt, d_ff_1_q, d_ff_2_q, d_ff_3_q, d_ff_4_q,
       d_ff_5_q, d_ff_6_q, d_ff_10_q, d_ff_11_q, not_1_out, not_2_out, not_3_out, not_4_out;
  wire [31:0] register_1_q, register_2_q;

  Comparator #(.width(32)) comparator_1 (.a(X_IN), .b(Y_IN), .eq(comparator_1_eq), .lt(comparator_1_lt));  // open: gt
  Comparator #(.mode("unsigned"), .width(32)) comparator_2 (.a(X_IN), .b(Y_IN), .lt(comparator_2_lt));  // open: gt, eq
  and and_1 (and_1_out, CLK, not_1_out);
  not not_1 (not_1_out, NOP);
  D_Flip_Flop d_ff_1 (.D(comparator_1_eq), .clk(not_2_out), .Q(d_ff_1_q));  // open: Qn, preset, reset
  D_Flip_Flop d_ff_2 (.D(comparator_1_lt), .clk(not_2_out), .Q(d_ff_2_q));  // open: Qn, preset, reset
  D_Flip_Flop d_ff_3 (.D(comparator_2_lt), .clk(not_2_out), .Q(d_ff_3_q));  // open: Qn, preset, reset
  not not_2 (not_2_out, and_1_out);
  Register #(.width(32)) RY (.D(Y_IN), .clk(and_1_out), .Q(Y));  // open: en, clr
  Register #(.width(32)) register_1 (.D(V_IN), .clk(and_1_out), .Q(register_1_q));  // open: en, clr
  LED C_EQ (.in(d_ff_1_q));
  LED C_LT (.in(d_ff_2_q));
  LED C_LTU (.in(d_ff_3_q));
  D_Flip_Flop d_ff_4 (.D(d_ff_1_q), .clk(and_1_out), .Q(d_ff_4_q));  // open: Qn, preset, reset
  D_Flip_Flop d_ff_5 (.D(d_ff_2_q), .clk(and_1_out), .Q(d_ff_5_q));  // open: Qn, preset, reset
  D_Flip_Flop d_ff_6 (.D(d_ff_3_q), .clk(and_1_out), .Q(d_ff_6_q));  // open: Qn, preset, reset
  not not_3 (not_3_out, and_1_out);
  Register #(.width(32)) register_2 (.D(register_1_q), .clk(not_3_out), .Q(register_2_q));  // open: en, clr
  D_Flip_Flop d_ff_7 (.D(d_ff_4_q), .clk(not_3_out), .Q(EQ));  // open: Qn, preset, reset
  D_Flip_Flop d_ff_8 (.D(d_ff_5_q), .clk(not_3_out), .Q(LT));  // open: Qn, preset, reset
  D_Flip_Flop d_ff_9 (.D(d_ff_6_q), .clk(not_3_out), .Q(LTU));  // open: Qn, preset, reset
  LED F_EQ (.in(EQ));
  LED F_LT (.in(LT));
  LED F_LTU (.in(LTU));
  D_Flip_Flop d_ff_10 (.D(LD), .clk(CLK), .Q(d_ff_10_q));  // open: Qn, preset, reset
  D_Flip_Flop d_ff_11 (.D(d_ff_10_q), .clk(not_4_out), .Q(d_ff_11_q));  // open: Qn, preset, reset
  not not_4 (not_4_out, CLK);
  Multiplexer #(.width(32)) multiplexer_1 (.in0(register_2_q), .in1(D_IN), .out(VAL), .sel(d_ff_11_q));
  LED LOAD (.in(d_ff_11_q));
  Register #(.trigger("high"), .width(32)) ALU (.D(VAL), .clk(1'b1));  // open: en, Q, clr
endmodule

module BranchController (
  input  [31:0] INSTR,
  input  EQ,
  input  LT,
  input  LTU,
  input  CLK,
  output LINK,
  output WE,
  output [4:0] RD,
  output JMP,
  output SUP
);

  wire and_2_out, and_3_out, d_ff_1_q, d_ff_2_q, d_ff_3_q, d_ff_4_q, d_ff_5_q, JMP_t, multiplexer_1_out,
       multiplexer_2_out, not_1_out, not_2_out, xor_1_out;

  Register #(.trigger("high"), .width(32)) V_INS (.D(INSTR), .clk(1'b1));  // open: en, Q, clr
  // PlaRom #(.Contents("1 0 2 1 0 2 2 1 0 2 0 2 2 1*4 0 1*5 2*4 1 1 0 1 0 0 1*4 0 0 1 0 0 1 0*3 1 0"), .\and (6), .outputs(3)) WBDEC: pin names not known; wires that end beside it: INSTR[6:2], 1'b0, {WE, JMP_t, LINK}
  Multiplexer multiplexer_1 (.in0(LT), .in1(LTU), .out(multiplexer_1_out), .sel(INSTR[13]));
  Multiplexer multiplexer_2 (.in0(EQ), .in1(multiplexer_1_out), .out(multiplexer_2_out), .sel(INSTR[14]));
  assign RD = {5{WE}} & INSTR[11:7];  // AND_Gate and_1, 5 bits wide
  LED COND (.in(xor_1_out));
  xor xor_1 (xor_1_out, INSTR[12], multiplexer_2_out);
  and and_2 (and_2_out, xor_1_out, JMP_t);
  and and_3 (and_3_out, JMP_t, LINK);
  Register #(.trigger("high"), .width(5)) V_RD (.D(RD), .clk(1'b1));  // open: en, Q, clr
  D_Flip_Flop d_ff_1 (.D(JMP), .clk(CLK), .Q(d_ff_1_q));  // open: Qn, preset, reset
  or or_1 (JMP, and_2_out, and_3_out);
  D_Flip_Flop d_ff_2 (.D(d_ff_1_q), .clk(not_1_out), .Q(d_ff_2_q));  // open: Qn, preset, reset
  not not_1 (not_1_out, CLK);
  D_Flip_Flop d_ff_3 (.D(d_ff_2_q), .clk(CLK), .Q(d_ff_3_q));  // open: Qn, preset, reset
  D_Flip_Flop d_ff_4 (.D(d_ff_3_q), .clk(not_2_out), .Q(d_ff_4_q));  // open: Qn, preset, reset
  not not_2 (not_2_out, CLK);
  D_Flip_Flop d_ff_5 (.D(d_ff_4_q), .clk(CLK), .Q(d_ff_5_q));  // open: Qn, preset, reset
  or or_2 (SUP, d_ff_1_q, d_ff_2_q, d_ff_3_q, d_ff_4_q, d_ff_5_q);

  // Other names for the same wires on the sheet: LNK = LINK

  // Notes on the sheet:
  //   OP[6:2]
  //   rd[11:7]
  //   funct3/imm [12]
  //   funct3/imm [13]
  //   funct3/imm [14]
endmodule

module OperandSequencer (
  input  CLK,
  input  NOP,
  input  WE,
  input  [4:0] RD,
  input  [4:0] RS1,
  input  [4:0] RS2,
  input  [4:0] WR,
  output [1:0] S1,
  output [1:0] S2
);

  wire A1, A2, A3, A4, A5, A6, A7, A8, A9, A10, A11, A12, A13, A14, A15, A16, A17, A18, A19, A20, A21, A22,
       A23, A24, A25, A26, A27, A28, A29, A30, A31, B1, B2, B3, B4, B5, B6, B7, B8, B9, B10, B11, B12, B13,
       B14, B15, B16, B17, B18, B19, B20, B21, B22, B23, B24, B25, B26, B27, B28, B29, B30, B31, not_1_out;
  wire [1:0] S1_t, S2_t, S3, S4, S5, S6, S7, S8, S9, S10, S11, S12, S13, S14, S15, S16, S17, S18, S19, S20,
       S21, S22, S23, S24, S25, S26, S27, S28, S29, S30, S31;

  Decoder #(.select(5)) decoder_1 (
    .out1(A1), .out2(A2), .out3(A3), .out4(A4), .out5(A5), .out6(A6), .out7(A7), .out8(A8), .out9(A9),
    .out10(A10), .out11(A11), .out12(A12), .out13(A13), .out14(A14), .out15(A15), .out16(A16), .out17(A17),
    .out18(A18), .out19(A19), .out20(A20), .out21(A21), .out22(A22), .out23(A23), .out24(A24), .out25(A25),
    .out26(A26), .out27(A27), .out28(A28), .out29(A29), .out30(A30), .out31(A31), .sel(WR), .en(WE));  // open: out0
  OperandCounter operandcounter_1 (.SEL(S8), .CE(not_1_out), .S0(A8), .S1(B8), .CLK(CLK));
  OperandCounter operandcounter_2 (.SEL(S16), .CE(not_1_out), .S0(A16), .S1(B16), .CLK(CLK));
  OperandCounter operandcounter_3 (.SEL(S24), .CE(not_1_out), .S0(A24), .S1(B24), .CLK(CLK));
  not not_1 (not_1_out, NOP);
  OperandCounter operandcounter_4 (.SEL(S1_t), .CE(not_1_out), .S0(A1), .S1(B1), .CLK(CLK));
  OperandCounter operandcounter_5 (.SEL(S9), .CE(not_1_out), .S0(A9), .S1(B9), .CLK(CLK));
  OperandCounter operandcounter_6 (.SEL(S17), .CE(not_1_out), .S0(A17), .S1(B17), .CLK(CLK));
  OperandCounter operandcounter_7 (.SEL(S25), .CE(not_1_out), .S0(A25), .S1(B25), .CLK(CLK));
  Decoder #(.enable("false"), .select(5)) decoder_2 (
    .out1(B1), .out2(B2), .out3(B3), .out4(B4), .out5(B5), .out6(B6), .out7(B7), .out8(B8), .out9(B9),
    .out10(B10), .out11(B11), .out12(B12), .out13(B13), .out14(B14), .out15(B15), .out16(B16), .out17(B17),
    .out18(B18), .out19(B19), .out20(B20), .out21(B21), .out22(B22), .out23(B23), .out24(B24), .out25(B25),
    .out26(B26), .out27(B27), .out28(B28), .out29(B29), .out30(B30), .out31(B31), .sel(RD));  // open: out0
  OperandCounter operandcounter_8 (.SEL(S2_t), .CE(not_1_out), .S0(A2), .S1(B2), .CLK(CLK));
  OperandCounter operandcounter_9 (.SEL(S10), .CE(not_1_out), .S0(A10), .S1(B10), .CLK(CLK));
  OperandCounter operandcounter_10 (.SEL(S18), .CE(not_1_out), .S0(A18), .S1(B18), .CLK(CLK));
  OperandCounter operandcounter_11 (.SEL(S26), .CE(not_1_out), .S0(A26), .S1(B26), .CLK(CLK));
  OperandCounter operandcounter_12 (.SEL(S3), .CE(not_1_out), .S0(A3), .S1(B3), .CLK(CLK));
  OperandCounter operandcounter_13 (.SEL(S11), .CE(not_1_out), .S0(A11), .S1(B11), .CLK(CLK));
  OperandCounter operandcounter_14 (.SEL(S19), .CE(not_1_out), .S0(A19), .S1(B19), .CLK(CLK));
  OperandCounter operandcounter_15 (.SEL(S27), .CE(not_1_out), .S0(A27), .S1(B27), .CLK(CLK));
  OperandCounter operandcounter_16 (.SEL(S4), .CE(not_1_out), .S0(A4), .S1(B4), .CLK(CLK));
  OperandCounter operandcounter_17 (.SEL(S12), .CE(not_1_out), .S0(A12), .S1(B12), .CLK(CLK));
  OperandCounter operandcounter_18 (.SEL(S20), .CE(not_1_out), .S0(A20), .S1(B20), .CLK(CLK));
  OperandCounter operandcounter_19 (.SEL(S28), .CE(not_1_out), .S0(A28), .S1(B28), .CLK(CLK));
  OperandCounter operandcounter_20 (.SEL(S5), .CE(not_1_out), .S0(A5), .S1(B5), .CLK(CLK));
  OperandCounter operandcounter_21 (.SEL(S13), .CE(not_1_out), .S0(A13), .S1(B13), .CLK(CLK));
  OperandCounter operandcounter_22 (.SEL(S21), .CE(not_1_out), .S0(A21), .S1(B21), .CLK(CLK));
  OperandCounter operandcounter_23 (.SEL(S29), .CE(not_1_out), .S0(A29), .S1(B29), .CLK(CLK));
  OperandCounter operandcounter_24 (.SEL(S6), .CE(not_1_out), .S0(A6), .S1(B6), .CLK(CLK));
  OperandCounter operandcounter_25 (.SEL(S14), .CE(not_1_out), .S0(A14), .S1(B14), .CLK(CLK));
  OperandCounter operandcounter_26 (.SEL(S22), .CE(not_1_out), .S0(A22), .S1(B22), .CLK(CLK));
  OperandCounter operandcounter_27 (.SEL(S30), .CE(not_1_out), .S0(A30), .S1(B30), .CLK(CLK));
  Register #(.trigger("high"), .width(2)) SEL_X (.D(S1), .clk(1'b1));  // open: en, Q, clr
  Multiplexer #(.select(5), .width(2)) multiplexer_1 (
    .in0(2'b00), .in1(S1_t), .in2(S2_t), .in3(S3), .in4(S4), .in5(S5), .in6(S6), .in7(S7), .in8(S8),
    .in9(S9), .in10(S10), .in11(S11), .in12(S12), .in13(S13), .in14(S14), .in15(S15), .in16(S16), .in17(S17),
    .in18(S18), .in19(S19), .in20(S20), .in21(S21), .in22(S22), .in23(S23), .in24(S24), .in25(S25),
    .in26(S26), .in27(S27), .in28(S28), .in29(S29), .in30(S30), .in31(S31), .out(S1), .sel(RS1));
  OperandCounter operandcounter_28 (.SEL(S7), .CE(not_1_out), .S0(A7), .S1(B7), .CLK(CLK));
  OperandCounter operandcounter_29 (.SEL(S15), .CE(not_1_out), .S0(A15), .S1(B15), .CLK(CLK));
  OperandCounter operandcounter_30 (.SEL(S23), .CE(not_1_out), .S0(A23), .S1(B23), .CLK(CLK));
  OperandCounter operandcounter_31 (.SEL(S31), .CE(not_1_out), .S0(A31), .S1(B31), .CLK(CLK));
  Multiplexer #(.select(5), .width(2)) multiplexer_2 (
    .in0(2'b00), .in1(S1_t), .in2(S2_t), .in3(S3), .in4(S4), .in5(S5), .in6(S6), .in7(S7), .in8(S8),
    .in9(S9), .in10(S10), .in11(S11), .in12(S12), .in13(S13), .in14(S14), .in15(S15), .in16(S16), .in17(S17),
    .in18(S18), .in19(S19), .in20(S20), .in21(S21), .in22(S22), .in23(S23), .in24(S24), .in25(S25),
    .in26(S26), .in27(S27), .in28(S28), .in29(S29), .in30(S30), .in31(S31), .out(S2), .sel(RS2));
  Register #(.trigger("high"), .width(2)) SEL_Y (.D(S2), .clk(1'b1));  // open: en, Q, clr
endmodule

module OperandMux (
  input  [1:0] SEL_X,
  input  [31:0] REG_X,
  input  [31:0] ALU_OUT,
  input  [31:0] MEM_IN,
  input  [31:0] REG_Y,
  input  [1:0] SEL_Y,
  input  CLK,
  output [31:0] OUT_X,
  output [31:0] OUT_Y
);

  wire decoder_1_out0, decoder_1_out1, decoder_1_out2, decoder_2_out0, decoder_2_out1, decoder_2_out2;
  wire [31:0] multiplexer_1_out, multiplexer_2_out;

  LED X_REG (.in(decoder_1_out0));
  LED X_ALU (.in(decoder_1_out1));
  LED X_MEM (.in(decoder_1_out2));
  Decoder #(.enable("false"), .select(2)) decoder_1 (
    .out0(decoder_1_out0), .out1(decoder_1_out1), .out2(decoder_1_out2), .sel(SEL_X));  // open: out3
  Register #(.width(32)) RX (.D(multiplexer_1_out), .clk(CLK), .Q(OUT_X));  // open: en, clr
  Multiplexer #(.select(2), .width(32)) multiplexer_1 (
    .in0(REG_X), .in1(ALU_OUT), .in2(MEM_IN), .in3({32{1'b0}}), .out(multiplexer_1_out), .sel(SEL_X));
  Register #(.width(32)) RY (.D(multiplexer_2_out), .clk(CLK), .Q(OUT_Y));  // open: en, clr
  Multiplexer #(.select(2), .width(32)) multiplexer_2 (
    .in0(REG_Y), .in1(ALU_OUT), .in2(MEM_IN), .in3({32{1'b0}}), .out(multiplexer_2_out), .sel(SEL_Y));
  LED Y_REG (.in(decoder_2_out0));
  Decoder #(.enable("false"), .select(2)) decoder_2 (
    .out0(decoder_2_out0), .out1(decoder_2_out1), .out2(decoder_2_out2), .sel(SEL_Y));  // open: out3
  LED Y_ALU (.in(decoder_2_out1));
  LED Y_MEM (.in(decoder_2_out2));
endmodule

module OperandCounter (
  input  CE,
  input  S0,
  input  S1,
  input  CLK,
  output [1:0] SEL
);

  wire and_1_out, or_1_out, or_2_out;

  Counter #(.max('h3), .width(2)) counter_1 (
    .load(or_1_out), .count(and_1_out), .clk(CLK), .D({1'b0, S1}), .Q(SEL));  // open: clr, up, carry
  and and_1 (and_1_out, CE, or_2_out);
  or or_1 (or_1_out, S0, S1);
  or or_2 (or_2_out, SEL[0], SEL[1]);
endmodule
